// Logisim project calculadora 12.circ as structural Verilog
module main (
  input  in_1,
  input  in_2,
  input  in_3,
  output out_4,
  output out_5
);

  wire and_1_out, and_2_out, and_3_out, xor_1_out;

  xor xor_1 (xor_1_out, in_1, in_2);
  and and_1 (and_1_out, in_1, in_2);
  and and_2 (and_2_out, in_1, in_3);
  and and_3 (and_3_out, in_2, in_3);
  xor xor_2 (out_4, xor_1_out, in_3);
  or or_1 (out_5, and_1_out, and_2_out, and_3_out);
endmodule

module subtrator (
  input  in_1,
  input  in_2,
  input  in_3,
  output out_4,
  output out_5
);

  wire and_1_out, and_2_out, and_3_out, not_1_out, not_2_out, xor_1_out;

  not not_1 (not_1_out, in_1);
  not not_2 (not_2_out, in_1);
  xor xor_1 (xor_1_out, in_1, in_2);
  and and_1 (and_1_out, not_1_out, in_2);
  and and_2 (and_2_out, not_2_out, in_3);
  and and_3 (and_3_out, in_2, in_3);
  xor xor_2 (out_4, xor_1_out, in_3);
  or or_1 (out_5, and_1_out, and_2_out, and_3_out);
endmodule

module Circuito (
  input  in_1,
  input  in_2,
  input  in_3,
  input  in_4,
  input  a0,
  input  [1:0] in_6,
  input  in_7,
  input  in_8,
  input  in_9,
  input  b0,
  input  in_11
);

  wire comparador_1_out_9, main_2_out_5, main_3_out_5, main_4_out_5, subtrator_2_out_5, subtrator_3_out_5,
       subtrator_4_out_5;
  wire [3:0] bit_extender_5_out, main_4_out_4, subtrator_4_out_4;
  wire [7:0] bit_extender_9_out, bit_extender_10_out, bit_extender_11_out, kj_1_out_9, multiplexer_1_out;

  main main_1 (.in_1(in_1), .in_2(in_7), .in_3(main_2_out_5), .out_4(main_4_out_4[3]));  // open: out_5
  main main_2 (.in_1(in_2), .in_2(in_8), .in_3(main_3_out_5), .out_4(main_4_out_4[2]), .out_5(main_2_out_5));
  main main_3 (.in_1(in_3), .in_2(in_9), .in_3(main_4_out_5), .out_4(main_4_out_4[1]), .out_5(main_3_out_5));
  main main_4 (.in_1(a0), .in_2(b0), .in_3(in_4), .out_4(main_4_out_4[0]), .out_5(main_4_out_5));
  subtrator subtrator_1 (
    .in_1(in_1), .in_2(in_7), .in_3(subtrator_2_out_5), .out_4(subtrator_4_out_4[3]));  // open: out_5
  subtrator subtrator_2 (
    .in_1(in_2), .in_2(in_8), .in_3(subtrator_3_out_5), .out_4(subtrator_4_out_4[2]),
    .out_5(subtrator_2_out_5));
  subtrator subtrator_3 (
    .in_1(in_3), .in_2(in_9), .in_3(subtrator_4_out_5), .out_4(subtrator_4_out_4[1]),
    .out_5(subtrator_3_out_5));
  subtrator subtrator_4 (.in_1(a0), .in_2(b0), .in_3(in_11), .out_4(subtrator_4_out_4[0]), .out_5(subtrator_4_out_5));
  Bit_Extender #(.in_width(1), .out_width(4)) bit_extender_1 (.in(main_4_out_4[3]));  // open: out
  Bit_Extender #(.in_width(1), .out_width(4)) bit_extender_2 (.in(main_4_out_4[2]));  // open: out
  Bit_Extender #(.in_width(1), .out_width(4)) bit_extender_3 (.in(main_4_out_4[1]));  // open: out
  Bit_Extender #(.in_width(1), .out_width(4)) bit_extender_4 (.in(main_4_out_4[0]));  // open: out
  assign bit_extender_5_out = {{3{1'b0}}, subtrator_4_out_4[3]};  // Bit_Extender bit_extender_5
  Bit_Extender #(.in_width(1), .out_width(4)) bit_extender_6 (.in(subtrator_4_out_4[2]));  // open: out
  Bit_Extender #(.in_width(1), .out_width(4)) bit_extender_7 (.in(subtrator_4_out_4[1]));  // open: out
  Bit_Extender #(.in_width(1), .out_width(4)) bit_extender_8 (.in(subtrator_4_out_4[0]));  // open: out
  assign bit_extender_9_out = {{4{1'b0}}, main_4_out_4};  // Bit_Extender bit_extender_9
  kj kj_1 (
    .in_1(a0), .in_2(in_3), .in_3(in_2), .in_4(in_1), .in_5(b0), .in_6(in_9), .in_7(in_8), .in_8(in_7),
    .out_9(kj_1_out_9[0]), .out_10(kj_1_out_9[1]), .out_11(kj_1_out_9[2]), .out_12(kj_1_out_9[3]),
    .out_13(kj_1_out_9[4]), .out_14(kj_1_out_9[5]), .out_15(kj_1_out_9[6]), .out_16(kj_1_out_9[7]));
  Comparador comparador_1 (
    .A0(a0), .B0(b0), .A1(in_3), .B1(in_9), .A2(in_2), .B2(in_8), .A3(in_1), .B3(b0),
    .out_9(comparador_1_out_9));
  assign bit_extender_10_out = {{4{1'b0}}, subtrator_4_out_4};  // Bit_Extender bit_extender_10
  assign bit_extender_11_out = {{7{1'b0}}, comparador_1_out_9};  // Bit_Extender bit_extender_11
  // Probe on bit_extender_9_out
  // Probe on bit_extender_10_out
  // Probe on kj_1_out_9
  // Probe on bit_extender_11_out
  // Probe on multiplexer_1_out
  Multiplexer #(.select(2), .width(8)) multiplexer_1 (
    .in0(bit_extender_9_out), .in1(kj_1_out_9), .in2(bit_extender_11_out), .in3(bit_extender_10_out),
    .out(multiplexer_1_out), .sel(in_6));  // open: en
endmodule

module Circuito1 (
  input  in_1,
  input  in_2,
  input  in_3,
  input  in_4,
  output out_5,
  output out_6
);

  wire and_1_out, and_2_out, or_1_out, xor_1_out, xor_2_out;

  xor xor_1 (xor_1_out, in_1, in_2);
  and and_1 (and_1_out, in_2, in_3);
  xor xor_2 (xor_2_out, in_1, in_4);
  or or_1 (or_1_out, in_2, in_3);
  xor xor_3 (out_5, xor_1_out, in_3);
  and and_2 (and_2_out, xor_2_out, or_1_out);
  or or_2 (out_6, and_1_out, and_2_out);
endmodule

module Multiplexador (
  input  in_1,
  input  in_2,
  output out_3,
  output out_4
);

  xor xor_1 (out_3, in_1, in_2);
  and and_1 (out_4, in_1, in_2);
endmodule

module kj (
  input  in_1,
  input  in_2,
  input  in_3,
  input  in_4,
  input  in_5,
  input  in_6,
  input  in_7,
  input  in_8,
  output out_9,
  output out_10,
  output out_11,
  output out_12,
  output out_13,
  output out_14,
  output out_15,
  output out_16
);

  wire and_2_out, and_3_out, and_4_out, and_5_out, and_6_out, and_7_out, and_8_out, and_9_out, and_10_out,
       and_11_out, and_12_out, and_13_out, and_14_out, and_15_out, and_16_out, multiplexador_1_out_4,
       multiplexador_2_out_3, multiplexador_3_out_3, multiplexador_4_out_3, multiplexador_5_out_4,
       multiplexador_6_out_3, multiplexador_7_out_3, multiplexador_8_out_4, multiplexador_9_out_3,
       multiplexador_10_out_3, multiplexador_11_out_4, multiplexador_12_out_3, multiplexador_13_out_4;

  and and_1 (out_9, in_1, in_5);
  and and_2 (and_2_out, in_1, in_6);
  and and_3 (and_3_out, in_5, in_2);
  Multiplexador multiplexador_1 (.in_1(and_2_out), .in_2(and_3_out), .out_3(out_10), .out_4(multiplexador_1_out_4));
  and and_4 (and_4_out, in_1, in_7);
  Multiplexador multiplexador_2 (
    .in_1(multiplexador_1_out_4), .in_2(and_4_out), .out_3(multiplexador_2_out_3));  // open: out_4
  and and_5 (and_5_out, in_5, in_3);
  and and_6 (and_6_out, in_2, in_6);
  Multiplexador multiplexador_3 (
    .in_1(multiplexador_2_out_3), .in_2(and_6_out), .out_3(multiplexador_3_out_3));  // open: out_4
  and and_7 (and_7_out, in_1, in_8);
  Multiplexador multiplexador_4 (
    .in_1(multiplexador_5_out_4), .in_2(and_7_out), .out_3(multiplexador_4_out_3));  // open: out_4
  Multiplexador multiplexador_5 (
    .in_1(multiplexador_3_out_3), .in_2(and_5_out), .out_3(out_11), .out_4(multiplexador_5_out_4));
  and and_8 (and_8_out, in_3, in_6);
  and and_9 (and_9_out, in_2, in_7);
  Multiplexador multiplexador_6 (
    .in_1(multiplexador_4_out_3), .in_2(and_9_out), .out_3(multiplexador_6_out_3));  // open: out_4
  and and_10 (and_10_out, in_2, in_8);
  and and_11 (and_11_out, in_4, in_5);
  Multiplexador multiplexador_7 (
    .in_1(multiplexador_6_out_3), .in_2(and_8_out), .out_3(multiplexador_7_out_3));  // open: out_4
  and and_12 (and_12_out, in_3, in_7);
  Multiplexador multiplexador_8 (
    .in_1(multiplexador_7_out_3), .in_2(and_11_out), .out_3(out_12), .out_4(multiplexador_8_out_4));
  and and_13 (and_13_out, in_6, in_4);
  and and_14 (and_14_out, in_3, in_8);
  Multiplexador multiplexador_9 (
    .in_1(multiplexador_8_out_4), .in_2(and_10_out), .out_3(multiplexador_9_out_3));  // open: out_4
  Multiplexador multiplexador_10 (
    .in_1(multiplexador_9_out_3), .in_2(and_12_out), .out_3(multiplexador_10_out_3));  // open: out_4
  and and_15 (and_15_out, in_4, in_7);
  Multiplexador multiplexador_11 (
    .in_1(multiplexador_10_out_3), .in_2(and_13_out), .out_3(out_13), .out_4(multiplexador_11_out_4));
  and and_16 (and_16_out, in_4, in_7);
  Multiplexador multiplexador_12 (
    .in_1(multiplexador_11_out_4), .in_2(and_14_out), .out_3(multiplexador_12_out_3));  // open: out_4
  Multiplexador multiplexador_13 (
    .in_1(multiplexador_12_out_3), .in_2(and_15_out), .out_3(out_14), .out_4(multiplexador_13_out_4));
  Multiplexador multiplexador_14 (.in_1(multiplexador_13_out_4), .in_2(and_16_out), .out_3(out_15), .out_4(out_16));
endmodule

module Comparador (
  input  A0,
  input  B0,
  input  A1,
  input  B1,
  input  A2,
  input  B2,
  input  A3,
  input  B3,
  output out_9
);

  wire xnor_1_out, xnor_2_out, xnor_3_out, xnor_4_out;

  xnor xnor_1 (xnor_1_out, A0, B0);
  xnor xnor_2 (xnor_2_out, A1, B1);
  xnor xnor_3 (xnor_3_out, A2, B2);
  xnor xnor_4 (xnor_4_out, A3, B3);
  and and_1 (out_9, xnor_1_out, xnor_2_out, xnor_3_out, xnor_4_out);
endmodule
